# Fritzing sketch схема (saved by Fritzing 0.9.5d)
circuit board: 25.085cm x 12.3117cm

parts:
  Компонент1 = Arduino Uno (Rev3)
  A1 = Arduino R4 Minima
  RS485_module1 = RS485 Module (MAX3485)
  RS485_module2 = RS485 Module (MAX3485)
  Компонент2 = HX711 Weighing Sensor Module
  Компонент3 = HX711 Weighing Sensor Module
  Компонент4 = RFID RC522
  S1 = Pushbutton [package="[THT]"]
  Mod1 = gy-906
  S2 = Pushbutton [package="[THT]"]
  J1 = Basic Servo
  J2 = Basic Servo

nets:
  N1: Компонент1.A0, S2.Pin_3, S2.Pin_4
  N2: Компонент1.D10_PWM/SS, RS485_module2.DI
  N3: Компонент1.D11_PWM/MOSI, RS485_module2.RO
  GND: Компонент1.GND, RS485_module2.GND, Компонент2.GND, S2.Pin_1, S2.Pin_2
  N4: Компонент1.D2, Компонент2.CK/TX
  N5: Компонент1.D3_PWM, Компонент2.DO/RX
  N6: Компонент1.D7, RS485_module2.RE, RS485_module2.DE
  VCC: Компонент1.5V, RS485_module2.VCC, Компонент2.VCC
  VCC_2: A1.Pin_4, Компонент4.VCC, Mod1.VIN
  VCC_3: A1.Pin_5, RS485_module1.VCC, Компонент3.VCC, J1.vcc, J2.vcc
  GND_2: A1.Pin_6, A1.Pin_7, A1.Pin_45, RS485_module1.GND, Компонент3.GND, Компонент4.GND, S1.Pin_1, S1.Pin_2, Mod1.GND, J1.gnd, J2.gnd
  N7: A1.Pin_31, RS485_module1.RO
  N8: A1.Pin_32, RS485_module1.DI
  N9: A1.Pin_33, Компонент3.CK/TX
  N10: A1.Pin_34, Компонент3.DO/RX
  N11: A1.Pin_35, A1.Pin_37, S1.Pin_3, S1.Pin_4
  N12: A1.Pin_36, Компонент4.RST
  N13: A1.Pin_38, RS485_module1.RE, RS485_module1.DE
  N14: A1.Pin_41, Компонент4.SDA
  N15: A1.Pin_42, Компонент4.MOSI
  N16: A1.Pin_43, Компонент4.MISO
  N17: A1.Pin_44, Компонент4.SCK
  N18: A1.Pin_47, Mod1.SDA
  N19: A1.Pin_48, Mod1.SCL
  N20: RS485_module1.A, RS485_module2.A
  N21: RS485_module1.B, RS485_module2.B

custom parts:
  Arduino R4 Minima: Introducing the Arduino UNO R4 Minima! This board boasts the RA4M1 microprocessor from Renesas, delivering increased processing power, expanded memory, and additional peripherals.
  RS485 Module (MAX3485): Commercially available RS485 to RS232 TTL Module
  gy-906: gy-906 Non-contact PIR I2C interface temperature sensor breakout board.
